# Fritzing sketch Recontruir RC pruebas (saved by Fritzing 0.9.3b)

parts:
  M1 = DC Motor
  Parça4 = Arduino Uno (Rev3) - ICSP
  S1 = H-Bridge with L298N
  BAT1 = BC9VPC [package=bc9vpc]

nets:
  N1: M1.pin_1, S1.M1-02
  N2: M1.pin_2, S1.M1-01
  N3: Parça4.D2, S1.IN1
  N4: Parça4.D3_PWM, S1.IN2
  5V: Parça4.5V, S1.5V
  GND: Parça4.GND, S1.GND, BAT1.V-
  N5: S1.12V, BAT1.V+

custom parts:
  H-Bridge with L298N: h-bridge
